# Fritzing sketch pressure (saved by Fritzing 1.0.1rc)
circuit board: 7.80476cm x 4.89048cm
breadboards: 1

parts:
  LLC1 = Logic Level Converter [package="Breakout board"]
  DC-DC = Mini-360 DC-DC Buck converter [package=THT]
  ADS1115 = Adafruit ADS1115 16Bit I2C ADC [part_number="Adafruit #1085"]
  D1_Mini = WeMos D1 Mini
  L2 = LED - 3mm [color="Green (570nm)" current=0.030A package="3 mm [THT]"]
  L1 = LED - 3mm [color="Red (633nm)" current=0.030A package="3 mm [THT]"]
  S1_+_- = Camdenboss CTB0158-3 [part_number=CTB0158-3 package=THT]
  S3_+_- = Camdenboss CTB0158-3 [part_number=CTB0158-3 package=THT]
  + = Camdenboss CTB0158-2 [part_number=CTB0158-2 package=THT]
  R2 = Resistor [tolerance=±5% resistance=220 package="1206 [SMD]"]
  R1 = Resistor [tolerance=±5% resistance=220 package="1206 [SMD]"]
  R4 = Resistor [tolerance=±5% resistance=100k package="1206 [SMD]"]
  R5 = Resistor [tolerance=±5% resistance=100k package="1206 [SMD]"]
  R3 = Resistor [tolerance=±5% resistance=100k package="1206 [SMD]"]
  S2_+_- = Camdenboss CTB0158-3 [part_number=CTB0158-3 package=THT]

nets:
  N1: LLC1.LV, D1_Mini.3V3
  N2: LLC1.L-GND, LLC1.H-GND, DC-DC.OUT-, ADS1115.GND, D1_Mini.G, L2.cathode, L1.cathode, S1_+_-.pin1, S1_+_-.terminal_1, S3_+_-.pin1, S3_+_-.terminal_1, R4.Pin_1, R5.Pin_1, R3.Pin_1, S2_+_-.pin1, S2_+_-.terminal_1
  N3: LLC1.LV3, D1_Mini.D1
  N4: LLC1.LV4, D1_Mini.D2
  N5: LLC1.HV4, ADS1115.SDA
  N6: LLC1.HV3, ADS1115.SCL
  VDD: LLC1.HV, DC-DC.OUT+, ADS1115.VDD, D1_Mini.5V, S1_+_-.pin2, S3_+_-.pin2, S2_+_-.pin2
  N7: DC-DC.IN-, +.pin1
  N8: DC-DC.IN+, +.pin2
  N9: ADS1115.AIN2, S3_+_-.pin3, R5.Pin_0
  N10: ADS1115.AIN1, R4.Pin_0, S2_+_-.pin3
  N11: ADS1115.AIN0, S1_+_-.pin3, R3.Pin_0
  N12: D1_Mini.D5, R1.Pin_0
  N13: D1_Mini.D6, R2.Pin_0
  N14: L2.anode, R2.Pin_1
  N15: L1.anode, R1.Pin_1

custom parts:
  Logic Level Converter: 5V to/from 3.3V logic level converter
  Mini-360 DC-DC Buck converter: Mini-360 DC-DC Buck converter. Tiny buck step down voltage converter, input voltage 4.75 to 23V output 1 to 17V adjustable. Available from ebay and the like.
  Adafruit ADS1115 16Bit I2C ADC: For microcontrollers without an analog-to-digital converter or when you want a higher-precision ADC, the ADS1115 provides 16-bit precision at 860 samples/second over I2C. The chip can be configured as 4 single-ended input channels, or two differential channels. As a nice bonus, it even includes a programmable gain amplifier, up to x16, to help boost up smaller single/differential signals to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
